# Fritzing sketch Untitled Sketch (saved by Fritzing 0.9.3b)
stripboards: 1

parts:
  元件1 = Arduino Pro Mini v13
  Q1 = TRANSISTOR_PNP [package=to-92]
  元件2 = InvenSense MPU6050
  DFRobot_DFPlayer_Mini1 = DFRobot DFPlayer Mini [part_number=DFR0299]
  Q2 = TRANSISTOR_PNP [package=to-92]
  Q3 = TRANSISTOR_PNP [package=to-92]
  Q4 = TRANSISTOR_PNP [package=to-92]
  Q5 = TRANSISTOR_PNP [package=to-92]
  Q6 = TRANSISTOR_PNP [package=to-92]
  R1 = Resistor [tolerance=±5% resistance=20 package="2512 [SMD]"]
  R1_2 = Resistor [tolerance=±5% resistance=20 package="2512 [SMD]"]
  R2 = Resistor [tolerance=±5% resistance=20 package="2512 [SMD]"]
  R4 = Resistor [tolerance=±5% resistance=20 package="2512 [SMD]"]
  R5 = Resistor [tolerance=±5% resistance=20 package="2512 [SMD]"]
  R6 = Resistor [tolerance=±5% resistance=20 package="2512 [SMD]"]
  BAT1 = Battery Holders [package=battery-aa]
  J1 = JST-03JQ-BT [part_number=JST-JQ-BT package=THT]
  SP1 = SPEAKER [package=pcb_mount_speaker]
  S1 = Momentary Switch [package=ksa_sealed_tac_switch]  # not connected
  LED1 = LEDs [package=led10mm]  # not connected

nets:
  N1: 元件1.A4, 元件2.SDA
  N2: 元件1.A5, 元件2.SCL
  N3: 元件1.RAW, DFRobot_DFPlayer_Mini1.VCC
  N4: 元件1.D11_PWM/MOSI, 元件1.D10_PWM/SS, 元件1.D9_PWM, 元件1.D6_PWM, 元件1.D5_PWM, 元件1.D3_PWM, R1.Pin_0, R1_2.Pin_0, R2.Pin_0, R4.Pin_0, R5.Pin_0, R6.Pin_0
  N5: 元件1.D8, DFRobot_DFPlayer_Mini1.TX
  N6: 元件1.D7, DFRobot_DFPlayer_Mini1.RX
  GND: 元件1.GND, 元件2.GND, DFRobot_DFPlayer_Mini1.GND-1, DFRobot_DFPlayer_Mini1.GND-2, BAT1.+, J1.pin1
  N7: Q1.E, Q2.E, Q3.E, Q4.E, Q5.E, Q6.E, R1.Pin_1, R1_2.Pin_1, R2.Pin_1, R4.Pin_1, R5.Pin_1, R6.Pin_1
  N8: Q1.B, Q2.B, Q3.B, Q4.B, Q5.B, Q6.B
  N9: Q1.C, 元件2.VCC, Q2.C, Q3.C, Q4.C, Q5.C, Q6.C, BAT1.-, J1.pin3
  N10: DFRobot_DFPlayer_Mini1.SPK_1, SP1.-
  N11: DFRobot_DFPlayer_Mini1.SPK_2, SP1.+
